// Logisim project Ctl_Flags_APSR.circ as structural Verilog: 1 circuit, main circuit Flags_APSR
module Flags_APSR (
  input  [3:0] Update_Mask,
  input  [3:0] Flags_In,
  input  Clk,
  input  Rst,
  output [3:0] Flags_Out
);

  Multiplexer #(.width(4)) multiplexer_1 (.in0(Update_Mask), .in1(Flags_In), .out(Flags_Out), .sel(Rst), .en(Clk));
endmodule
