// Logisim project Ctl_Load_Store.circ as structural Verilog: 1 circuit, main circuit Load_Store
module Load_Store (
  input  Enable,
  input  [15:0] Instruction,
  input  Clk,
  input  Reset,
  input  [31:0] Stack_Pointer,
  output Store,
  output Load,
  output PC_Hold,
  output [2:0] Rmd,
  output [31:0] RAM_Addr
);

  wire and_1_out, d_ff_1_q, Load_t, not_1_out, PC_Hold_t;
  wire [2:0] rmd_t;
  wire [7:0] shifter_1_out;
  wire [31:0] bit_extender_1_out, ram_addr_t;

  Shifter shifter_1 (.in(Instruction[7:0]), .\dist (3'b010), .out(shifter_1_out));
  assign bit_extender_1_out = {{24{shifter_1_out[7]}}, shifter_1_out};  // Bit_Extender bit_extender_1
  Adder #(.width(32)) adder_1 (.a(Stack_Pointer), .b(bit_extender_1_out), .out(ram_addr_t));  // open: cin, cout
  Pull_Resistor pull_resistor_1 (.node(Store));
  not not_1 (not_1_out, Instruction[11]);
  assign Store = Enable ? not_1_out : 1'bz;  // Controlled_Buffer controlled_buffer_1
  Pull_Resistor pull_resistor_2 (.node(Load));
  assign Load = Enable ? Load_t : 1'bz;  // Controlled_Buffer controlled_buffer_2
  Pull_Resistor pull_resistor_3 (.node(PC_Hold));
  assign PC_Hold = Enable ? PC_Hold_t : 1'bz;  // Controlled_Buffer controlled_buffer_3
  Pull_Resistor pull_resistor_4 (.node(Rmd));
  assign Rmd = Enable ? rmd_t : 3'bz;  // Controlled_Buffer controlled_buffer_4
  Pull_Resistor pull_resistor_5 (.node(RAM_Addr));
  assign RAM_Addr = Enable ? ram_addr_t : 32'bz;  // Controlled_Buffer controlled_buffer_5
  D_Flip_Flop d_ff_1 (.D(and_1_out), .clk(Clk), .Q(d_ff_1_q), .reset(Reset));  // open: Qn, preset
  and and_1 (and_1_out, d_ff_1_q, Instruction[11]);
  and and_2 (Load_t, Instruction[11], d_ff_1_q);
  and and_3 (PC_Hold_t, d_ff_1_q, Instruction[11]);

  // Other names for the same wires on the sheet: imm8[7:0] = Instruction[7:0]; Rt[2:0] = Instruction[10:8];
  //   Bit_11 = Instruction[11]; SP[31:0] = Stack_Pointer

  // Notes on the sheet:
  //   Instruction: pull=down
  //   store / load
  //   Delay load and hold PC for 1 cycle for the RAM to send out requested data 
endmodule
