// Logisim project Ctl_Opcode_Decoder.circ as structural Verilog: 1 circuit, main circuit Opcode_Decoder
module Opcode_Decoder (
  input  [5:0] Opcode,
  output Shift,
  output Data_Processing,
  output Load_Store,
  output SP_Address,
  output Conditional
);


  assign Conditional = Opcode[4];
  assign Data_Processing = Opcode[1];
  assign Load_Store = Opcode[2];
  assign Shift = Opcode[0];
  assign SP_Address = Opcode[3];
  // also tied to GND on the sheet: Opcode[5]

  // Notes on the sheet:
  //   Shift, add, sub, mov
  //   Load/Store
  //   SP Address
  //   Conditional branch
  //   Data Processing
endmodule
